# Fritzing sketch USB_Over_IP (saved by Fritzing 1.0.5)

parts:
  MH-CD1 = MH-CD42
  MCU1 = Raspberry Pi Zero
  Bat1 = battery_holder_single_18650
  S1 = Pushbutton [package="[THT]"]
  D1 = LED_BARGRAPH_8 [package=led_bargaph_8]
  R8 = Resistor [tolerance=±5% power=0.25W resistance=330 package=THT]  # not connected
  R9 = Resistor [tolerance=±5% power=0.25W resistance=330 package=THT]  # not connected
  R10 = Resistor [tolerance=±5% power=0.25W resistance=330 package=THT]  # not connected
  R11 = Resistor [tolerance=±5% power=0.25W resistance=330 package=THT]  # not connected
  R12 = Resistor [tolerance=±5% power=0.25W resistance=330 package=THT]  # not connected
  R17 = Resistor [tolerance=±5% power=0.25W resistance=330 package=THT]  # not connected
  R19 = Resistor [tolerance=±5% power=0.25W resistance=330 package=THT]  # not connected
  R21 = Resistor [tolerance=±5% power=0.25W resistance=330 package=THT]
  X1 = USB Connectors [package=usb-a-s]  # not connected

nets:
  N1: MH-CD1.BAT, Bat1.+#1
  N2: MH-CD1.GND#4, Bat1.+#0
  N3: MH-CD1.KEY, S1.Pin_4
  N4: MCU1.pin_14, MCU1.pin_30, R21.Pin_0
  N5: MCU1.pin_29, D1.B_A
  N6: MCU1.pin_31, D1.A_A
  N7: MCU1.pin_32, D1.D_A
  N8: MCU1.pin_33, D1.C_A
  N9: MCU1.pin_36, D1.F_A
  N10: MCU1.pin_37, D1.E_A
  N11: MCU1.pin_38, D1.G_A
  N12: MCU1.pin_40, D1.H_A

notes:
  5,6,13,12,26,16,20,21
  Şarj içi 5V girişi

custom parts:
  MH-CD42: The MH-CD42 is a compact module designed for use with a single (1S) Li-Ion or Li-Po cell, or multiple cells connected in parallel. At its core, the module uses the IP5306 power management chip, a robust solution for efficient power regulation both for charging and for discharging. This 16x25mm module integrates all necessary components for building power banks, portable chargers, or adding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
  battery_holder_single_18650: single 18650 battery holder
  LED_BARGRAPH_8: 8-Segment LED Bar Graph
